# Fritzing sketch ENC28J60 (saved by Fritzing 0.7.10b)
breadboards: 2

parts:
  ENC28J60 = ENC28J60 [chip_label=ENC28J60 package="DIP (Dual Inline) [THT]"]
  C3 = Tantalum Capacitor [capacitance="1 μF" package="100 mil [THT, tantalum]"]
  R1 = Resistor [tolerance=±5% resistance=10k package=THT]
  R2 = Resistor [tolerance=±5% resistance=10k package=THT]
  R10 = Resistor [tolerance=±5% resistance=2.7k package=THT]
  R3 = Resistor [tolerance=±5% resistance=1k package=THT]
  R4 = Resistor [tolerance=±5% resistance=1k package=THT]
  Y1 = Resonator [package=THT]
  C2 = Ceramic Capacitor [capacitance=18pF package="100 mil [THT, multilayer]"]
  C1 = Ceramic Capacitor [capacitance=18pF package="100 mil [THT, multilayer]"]
  TRXCOM1 = RJ45-TRXCOM [part_number=TRJ0011BANL]

nets:
  N1: ENC28J60.pin1, C3.+
  GND: ENC28J60.pin2, ENC28J60.pin11, ENC28J60.pin18, ENC28J60.pin21, ENC28J60.pin22, C3.-, R10.Pin_1, TRXCOM1.Yellow_Kathode_-, TRXCOM1.Green_Kathode_-, TRXCOM1.Sheeld
  N2: ENC28J60.pin9, R1.Pin_0
  N3: ENC28J60.pin10, R2.Pin_0
  N4: ENC28J60.pin14, R10.Pin_0
  N5: ENC28J60.pin23, Y1.1, C1.0
  N6: ENC28J60.pin24, Y1.0, C2.0
  N7: ENC28J60.pin26, R4.Pin_1
  N8: ENC28J60.pin27, R3.Pin_1
  5V: ENC28J60.pin28, R1.Pin_1, R2.Pin_1
  N9: R3.Pin_0, TRXCOM1.Green_Anode_+
  N10: R4.Pin_0, TRXCOM1.Yellow_Anode_+
  N11: C2.1, C1.1

custom parts:
  ENC28J60: A DIP stand-in part for whatever IC you want. With 28 pins on a 300mil dual inline package (DIP) footprint.
